// Logisim project Relogio.circ as structural Verilog: 6 circuits, main circuit main
module main (
);

  wire _0_59_2_clk_seguinte, _0_59_clk_seguinte, INICIAR_out, RESET_out, TROCAR_AM_PM_out;
  wire [3:0] _0_24_12_12_dezena, _0_24_12_12_unidade, _0_59_2_dezena, _0_59_2_unidade, _0_59_dezena,
       _0_59_unidade;

  Button TROCAR_AM_PM (.out(TROCAR_AM_PM_out));
  Button RESET (.out(RESET_out));
  Hex_Digit_Display hex_digit_display_1 (.value(_0_24_12_12_dezena));  // open: dp
  Hex_Digit_Display hex_digit_display_2 (.value(_0_59_dezena));  // open: dp
  Hex_Digit_Display hex_digit_display_3 (.value(_0_24_12_12_unidade));  // open: dp
  AMPM_24H _0_24_12_12 (
    .DEZENA(_0_24_12_12_dezena), .AMPM_e_24(TROCAR_AM_PM_out), .UNIDADE(_0_24_12_12_unidade),
    .CLK(_0_59_clk_seguinte), .RESET(RESET_out));
  Hex_Digit_Display hex_digit_display_4 (.value(_0_59_unidade));  // open: dp
  Hex_Digit_Display hex_digit_display_5 (.value(_0_59_2_dezena));  // open: dp
  cont_0_a_59 _0_59 (
    .Dezena(_0_59_dezena), .CLK_Seguinte(_0_59_clk_seguinte), .Unidade(_0_59_unidade),
    .CLK(_0_59_2_clk_seguinte), .RESET(RESET_out));
  Hex_Digit_Display hex_digit_display_6 (.value(_0_59_2_unidade));  // open: dp
  cont_0_a_59 _0_59_2 (
    .Dezena(_0_59_2_dezena), .CLK_Seguinte(_0_59_2_clk_seguinte), .Unidade(_0_59_2_unidade),
    .CLK(INICIAR_out), .RESET(RESET_out));
  Clock INICIAR (.out(INICIAR_out));
endmodule

module cont_0_a_9 (
  input  CLK,
  input  Reset,
  output [3:0] Saida,
  output CLK_SEGUINTE
);

  wire OR_out;
  wire [3:0] adder_1_out;

  Hex_Digit_Display hex_digit_display_1 (.value(Saida));  // open: dp
  Register #(.width(4)) register_1 (.D(adder_1_out), .Q(Saida), .clk(CLK), .clr(OR_out));  // open: en
  or OR (OR_out, CLK_SEGUINTE, Reset);
  Adder #(.width(4)) adder_1 (.a(Saida), .b(4'b0001), .out(adder_1_out));  // open: cin, cout
  nor NOR (CLK_SEGUINTE, Saida[0], ~Saida[1], Saida[2], ~Saida[3]);  // NOR_Gate
endmodule

module cont_0_a_59 (
  input  CLK,
  input  RESET,
  output [3:0] Unidade,
  output [3:0] Dezena,
  output CLK_Seguinte
);

  wire _0A9_2_clk_seguinte, or_1_out;

  Hex_Digit_Display hex_digit_display_1 (.value(Dezena));  // open: dp
  cont_0_a_9 _0A9 (.CLK(_0A9_2_clk_seguinte), .Reset(or_1_out), .Saida(Dezena));  // open: CLK_SEGUINTE
  Hex_Digit_Display hex_digit_display_2 (.value(Unidade));  // open: dp
  cont_0_a_9 _0A9_2 (.CLK(CLK), .Reset(or_1_out), .Saida(Unidade), .CLK_SEGUINTE(_0A9_2_clk_seguinte));
  nor nor_1 (CLK_Seguinte, Dezena[3], ~Dezena[2], ~Dezena[1], Dezena[0], Unidade[3], Unidade[2], Unidade[1], Unidade[0]);  // NOR_Gate
  or or_1 (or_1_out, CLK_Seguinte, RESET);
endmodule

module count_0_a_23 (
  input  CLK,
  input  RESET,
  output [3:0] Unidade,
  output [3:0] Dezena,
  output CLK_Seguinte
);

  wire _0A9_2_clk_seguinte, or_1_out;

  Hex_Digit_Display hex_digit_display_1 (.value(Dezena));  // open: dp
  cont_0_a_9 _0A9 (.CLK(_0A9_2_clk_seguinte), .Reset(or_1_out), .Saida(Dezena));  // open: CLK_SEGUINTE
  Hex_Digit_Display hex_digit_display_2 (.value(Unidade));  // open: dp
  cont_0_a_9 _0A9_2 (.CLK(CLK), .Reset(or_1_out), .Saida(Unidade), .CLK_SEGUINTE(_0A9_2_clk_seguinte));
  nor nor_1 (CLK_Seguinte, Dezena[3], Dezena[2], ~Dezena[1], Dezena[0], Unidade[3], ~Unidade[2], Unidade[1], Unidade[0]);  // NOR_Gate
  or or_1 (or_1_out, CLK_Seguinte, RESET);
endmodule

module count_12x12 (
  input  CLK,
  input  RESET,
  output [3:0] DEZENA,
  output [3:0] UNIDADE
);

  wire _0a9_2_clk_seguinte, NOR_2_out, NOR_out, OR_out;
  wire [3:0] _0a9_2_saida, _0a9_saida;

  Hex_Digit_Display hex_digit_display_1 (.value(DEZENA));  // open: dp
  Multiplexer #(.width(4), .enable("false")) multiplexer_1 (
    .in0(_0a9_saida), .in1(4'b0001), .out(DEZENA), .sel(NOR_2_out));
  cont_0_a_9 _0a9 (.CLK(_0a9_2_clk_seguinte), .Reset(OR_out), .Saida(_0a9_saida));  // open: CLK_SEGUINTE
  Hex_Digit_Display hex_digit_display_2 (.value(UNIDADE));  // open: dp
  Multiplexer #(.width(4), .enable("false")) multiplexer_2 (
    .in0(_0a9_2_saida), .in1(4'b0010), .out(UNIDADE), .sel(NOR_2_out));
  cont_0_a_9 _0a9_2 (.CLK(CLK), .Reset(OR_out), .Saida(_0a9_2_saida), .CLK_SEGUINTE(_0a9_2_clk_seguinte));
  nor NOR (NOR_out, _0a9_saida[3], _0a9_saida[2], _0a9_saida[1], ~_0a9_saida[0], _0a9_2_saida[3], _0a9_2_saida[2], ~_0a9_2_saida[1], _0a9_2_saida[0]);  // NOR_Gate
  or OR (OR_out, NOR_out, RESET);
  nor NOR_2 (NOR_2_out, _0a9_2_saida[0], _0a9_2_saida[1], _0a9_2_saida[2], _0a9_2_saida[3], _0a9_saida[0], _0a9_saida[1], _0a9_saida[2], _0a9_saida[3]);
endmodule

module AMPM_24H (
  input  AMPM_e_24,
  input  CLK,
  input  RESET,
  output [3:0] DEZENA,
  output [3:0] UNIDADE
);

  wire d_ff_1_q, subtractor_1_out;
  wire [3:0] _0_23_dezena, _0_23_unidade, _12x12_dezena, _12x12_unidade;

  D_Flip_Flop d_ff_1 (.clk(AMPM_e_24), .D(subtractor_1_out), .Q(d_ff_1_q));  // open: Qn, preset, en, reset
  Subtractor #(.width(1)) subtractor_1 (.a(d_ff_1_q), .b(1'b1), .out(subtractor_1_out));  // open: bin, bout
  Hex_Digit_Display hex_digit_display_1 (.value(DEZENA));  // open: dp
  Multiplexer #(.width(4), .enable("false")) multiplexer_1 (
    .in0(_0_23_dezena), .in1(_12x12_dezena), .out(DEZENA), .sel(d_ff_1_q));
  count_0_a_23 _0_23 (.Dezena(_0_23_dezena), .Unidade(_0_23_unidade), .CLK(CLK), .RESET(RESET));  // open: CLK_Seguinte
  Hex_Digit_Display hex_digit_display_2 (.value(UNIDADE));  // open: dp
  Multiplexer #(.width(4), .enable("false")) multiplexer_2 (
    .in0(_0_23_unidade), .in1(_12x12_unidade), .out(UNIDADE), .sel(d_ff_1_q));
  count_12x12 _12x12 (.DEZENA(_12x12_dezena), .UNIDADE(_12x12_unidade), .CLK(CLK), .RESET(RESET));
endmodule
